# Fritzing sketch smartPlantFritzingLayout (saved by Fritzing 1.0.0rc)
breadboards: 2

parts:
  A1 = Particle - Photon2
  Part1 = MQ-131 breakout
  Grove1 = Grove Dust Sensor
  J1 = Camdenboss CTB0158-3 [part_number=CTB0158-3 package=THT]
  J3 = Camdenboss CTB0158-3 [part_number=CTB0158-3 package=THT]
  Chirp!_Soil_Moisture_Sensor1 = Chirp! Soil Moisture Sensor v2.7.3
  Relay1 = Relay - 6 pins [package="DIP (Dual Inline) [THT]"]
  OLED_I2C1 = OLED 128x64 I2C Monochrome Display
  M1 = BMP280

nets:
  VCC: A1.Pin_2, A1.Pin_31, Chirp!_Soil_Moisture_Sensor1.pin_2, Relay1.VCC, OLED_I2C1.VDD, M1.VIN
  GND: A1.Pin_4, A1.Pin_32, Chirp!_Soil_Moisture_Sensor1.pin_4, Relay1.GND, OLED_I2C1.GND, M1.GND
  N1: A1.Pin_6, Chirp!_Soil_Moisture_Sensor1.Pin_0
  N2: A1.Pin_7, Grove1.NC, J3.pin1
  N3: A1.Pin_8, Part1.AO, J1.pin3
  N4: A1.Pin_13, Relay1.IN
  N5: A1.Pin_17, OLED_I2C1.SDA, M1.SDA
  N6: A1.Pin_18, OLED_I2C1.SCK, M1.SCL
  N7: A1.Pin_26, Grove1.VCC, J3.pin2, Relay1.ON
  N8: Part1.VCC, J1.pin1
  N9: Part1.GND, J1.pin2
  N10: Grove1.GND, J3.pin3

custom parts:
  Particle - Photon2: The Photon 2 is a microcontroller and Wi-Fi networking developed by particle. Features: 802.11a/b/g/n Wi-Fi, 2.4 GHz and 5 GHz Integrated PCB antenna Integrated U.FL connector for external antenna Integrated RF switch BLE 5 using same antenna as Wi-Fi Realtek RTL8721DM MCU ARM Cortex M33 CPU, 200 MHz 2048 KB (2 MB) user application maximum size 3072 KB (3 MB) of RAM available to user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
  MQ-131 breakout: SKU: 101282
  Grove Dust Sensor: PPD42 Grove Dust Sensor
  Relay - 6 pins: A DIP stand-in part for whatever IC you want. With 6 pins on a 900mil dual inline package (DIP) footprint.
  BMP280: Temperature Humidity Barometric presure Sensor, I2C
